// Logisim project Ativ04.circ as structural Verilog
module Decodificador (
  input  E1,
  input  E2,
  input  E3,
  output AND,
  output OR,
  output NOT,
  output NAND,
  output NOR,
  output XOR,
  output XNOR,
  output SOMADOR
);

  wire not_1_out, not_2_out, not_3_out, not_4_out, not_5_out, not_6_out, not_7_out, not_8_out, not_9_out,
       not_10_out, not_11_out, not_12_out;

  not not_1 (not_1_out, E3);
  not not_2 (not_2_out, E2);
  not not_3 (not_3_out, E2);
  not not_4 (not_4_out, E3);
  not not_5 (not_5_out, E1);
  not not_6 (not_6_out, E1);
  not not_7 (not_7_out, E3);
  not not_8 (not_8_out, E1);
  not not_9 (not_9_out, E2);
  not not_10 (not_10_out, E1);
  not not_11 (not_11_out, E2);
  not not_12 (not_12_out, E3);
  and and_1 (AND, E1, E2, E3);
  and and_2 (OR, E1, E2, not_1_out);
  and and_3 (NOT, E1, not_2_out, E3);
  and and_4 (NAND, E1, not_3_out, not_4_out);
  and and_5 (NOR, not_5_out, E2, E3);
  and and_6 (XOR, not_6_out, E2, not_7_out);
  and and_7 (XNOR, not_8_out, not_9_out, E3);
  and and_8 (SOMADOR, not_10_out, not_11_out, not_12_out);
endmodule

// Unidade Logica
module UnidadeLogica (
  input  A,
  input  B,
  input  AND,
  input  NAND,
  input  OR,
  input  NOR,
  input  XOR,
  input  XNOR,
  input  AND_2,
  output AND_3,
  output NAND_2,
  output OR_2,
  output NOR_2,
  output XOR_2,
  output XNOR_2,
  output NOT,
  output Sa,
  output Sb
);

  wire and_1_out, nand_1_out, nor_1_out, not_1_out, or_1_out, xnor_1_out, xor_1_out;

  and and_1 (and_1_out, A, B);
  nand nand_1 (nand_1_out, A, B);
  or or_1 (or_1_out, A, B);
  nor nor_1 (nor_1_out, A, B);
  xor xor_1 (xor_1_out, A, B);
  xnor xnor_1 (xnor_1_out, B, A);
  not not_1 (not_1_out, B);
  and u_and_2 (AND_3, and_1_out, AND);
  and u_and_3 (NAND_2, nand_1_out, NAND);
  and and_4 (OR_2, or_1_out, OR);
  and and_5 (NOR_2, nor_1_out, NOR);
  and and_6 (XOR_2, xor_1_out, XOR);
  and and_7 (XNOR_2, xnor_1_out, XNOR);
  and and_8 (NOT, not_1_out, AND_2);

  assign Sa = B;
  assign Sb = B;
endmodule

// Soma
module Somador (
  input  A,
  input  B,
  input  C,
  input  Carry_in,
  input  OP,
  output S,
  output Carry_Out
);

  wire and_1_out, and_2_out, and_3_out, xor_1_out, xor_2_out, xor_3_out;

  xor xor_1 (xor_1_out, A, OP);
  xor xor_2 (xor_2_out, B, Carry_in);
  and and_1 (and_1_out, B, C, Carry_in);
  and and_2 (and_2_out, B, C, xor_1_out);
  and and_3 (and_3_out, Carry_in, C, xor_1_out);
  xor xor_3 (xor_3_out, A, xor_2_out);
  and and_4 (S, xor_3_out, C);
  or or_1 (Carry_Out, and_1_out, and_2_out, and_3_out);
endmodule

module ULA1bit (
  input  Carry_In,
  input  A,
  input  B,
  input  E1,
  input  E2,
  input  E3,
  input  OP,
  output Out_Put,
  output Carry_Out
);

  wire decodificador_1_and, decodificador_1_nand, decodificador_1_nor, decodificador_1_not,
       decodificador_1_or, decodificador_1_somador, decodificador_1_xnor, decodificador_1_xor, somador_1_s,
       unidadelogica_1_and_3, unidadelogica_1_nand_2, unidadelogica_1_nor_2, unidadelogica_1_not,
       unidadelogica_1_or_2, unidadelogica_1_sa, unidadelogica_1_sb, unidadelogica_1_xnor_2,
       unidadelogica_1_xor_2;

  Decodificador decodificador_1 (
    .E1(E1), .E2(E2), .E3(E3), .AND(decodificador_1_and), .OR(decodificador_1_or), .NOT(decodificador_1_not),
    .NAND(decodificador_1_nand), .NOR(decodificador_1_nor), .XOR(decodificador_1_xor),
    .XNOR(decodificador_1_xnor), .SOMADOR(decodificador_1_somador));
  UnidadeLogica unidadelogica_1 (
    .A(A), .B(B), .Sa(unidadelogica_1_sa), .Sb(unidadelogica_1_sb), .AND(decodificador_1_and),
    .NAND(decodificador_1_nand), .OR(decodificador_1_or), .NOR(decodificador_1_nor),
    .XOR(decodificador_1_xor), .XNOR(decodificador_1_xnor), .AND_2(decodificador_1_not),
    .AND_3(unidadelogica_1_and_3), .NAND_2(unidadelogica_1_nand_2), .OR_2(unidadelogica_1_or_2),
    .NOR_2(unidadelogica_1_nor_2), .XOR_2(unidadelogica_1_xor_2), .XNOR_2(unidadelogica_1_xnor_2),
    .NOT(unidadelogica_1_not));
  Somador somador_1 (
    .A(unidadelogica_1_sa), .B(unidadelogica_1_sb), .C(decodificador_1_somador), .Carry_in(Carry_In),
    .OP(OP), .S(somador_1_s), .Carry_Out(Carry_Out));
  or or_1 (Out_Put, unidadelogica_1_not, unidadelogica_1_and_3, unidadelogica_1_nand_2, unidadelogica_1_or_2, unidadelogica_1_nor_2, unidadelogica_1_xor_2, unidadelogica_1_xnor_2, somador_1_s);
endmodule

module ULA8bits (
  input  A8,
  input  A8_2,
  input  A8_3,
  input  A8_4,
  input  A8_5,
  input  A8_6,
  input  A8_7,
  input  A8_8,
  input  B8,
  input  B8_2,
  input  B8_3,
  input  B8_4,
  input  B8_5,
  input  B8_6,
  input  B8_7,
  input  B8_8,
  input  OP,
  input  E1,
  input  E2,
  input  E3,
  input  in_21,
  input  in_22,
  input  in_23,
  input  in_24,
  input  in_25,
  input  in_26,
  output OverFlow,
  output out_28,
  output out_29,
  output out_30,
  output out_31,
  output out_32,
  output out_33,
  output out_34,
  output out_35,
  output out_36,
  output out_37
);

  wire ula1bit_3_out_put, ula1bit_4_out_put, ula1bit_5_out_put, ula1bit_6_out_put, ula1bit_7_out_put,
       ula1bit_8_out_put, ula1bit_9_out_put;

  ULA1bit ula1bit_1 (
    .A(in_21), .B(in_22), .E1(in_23), .E2(in_24), .E3(in_26), .Carry_In(1'b0), .OP(in_25),
    .Carry_Out(out_37), .Out_Put(out_36));
  ULA1bit ula1bit_2 (
    .A(A8), .B(B8), .E1(E1), .E2(E2), .E3(E3), .Carry_In(ula1bit_3_out_put), .OP(OP), .Carry_Out(out_28),
    .Out_Put(OverFlow));
  ULA1bit ula1bit_3 (
    .A(A8_2), .B(B8_2), .E1(E1), .E2(E2), .E3(E3), .Carry_In(ula1bit_4_out_put), .OP(OP), .Carry_Out(out_29),
    .Out_Put(ula1bit_3_out_put));
  ULA1bit ula1bit_4 (
    .A(A8_3), .B(B8_3), .E1(E1), .E2(E2), .E3(E3), .Carry_In(ula1bit_5_out_put), .OP(OP), .Carry_Out(out_30),
    .Out_Put(ula1bit_4_out_put));
  ULA1bit ula1bit_5 (
    .A(A8_4), .B(B8_4), .E1(E1), .E2(E2), .E3(E3), .Carry_In(ula1bit_6_out_put), .OP(OP), .Carry_Out(out_31),
    .Out_Put(ula1bit_5_out_put));
  ULA1bit ula1bit_6 (
    .A(A8_5), .B(B8_5), .E1(E1), .E2(E2), .E3(E3), .Carry_In(ula1bit_7_out_put), .OP(OP), .Carry_Out(out_32),
    .Out_Put(ula1bit_6_out_put));
  ULA1bit ula1bit_7 (
    .A(A8_6), .B(B8_6), .E1(E1), .E2(E2), .E3(E3), .Carry_In(ula1bit_8_out_put), .OP(OP), .Carry_Out(out_33),
    .Out_Put(ula1bit_7_out_put));
  ULA1bit ula1bit_8 (
    .A(A8_7), .B(B8_7), .E1(E1), .E2(E2), .E3(E3), .Carry_In(ula1bit_9_out_put), .OP(OP), .Carry_Out(out_34),
    .Out_Put(ula1bit_8_out_put));
  ULA1bit ula1bit_9 (
    .A(A8_8), .B(B8_8), .E1(E1), .E2(E2), .E3(E3), .Carry_In(1'b0), .OP(OP), .Carry_Out(out_35),
    .Out_Put(ula1bit_9_out_put));
endmodule
