// Logisim project Ulas.circ as structural Verilog
module Decodificador (
  input  in_1,
  input  in_2,
  input  in_3,
  input  in_4,
  input  in_5,
  output out_6,
  output out_7
);

  // XOR_Gate xor_1 is placed but not wired
  // AND_Gate and_1 is placed but not wired
  // AND_Gate and_2 is placed but not wired
  // AND_Gate and_3 is placed but not wired
  // XOR_Gate xor_2 is placed but not wired
  // XOR_Gate xor_3 is placed but not wired
  // AND_Gate and_4 is placed but not wired
  // OR_Gate or_1 is placed but not wired
endmodule
