// Logisim project Fig 3.5.circ as structural Verilog: 1 circuit, main circuit main
module main (
  input  in_1,
  input  in_2,
  input  in_3,
  input  in_4,
  input  in_5,
  input  in_6,
  output out_7,
  output out_8
);

  wire and_1_out, and_2_out, or_2_out;

  and and_1 (and_1_out, in_1, in_3);
  and and_2 (and_2_out, in_1, in_6);
  or or_1 (out_8, and_1_out, and_2_out);
  or or_2 (or_2_out, in_4, in_5);
  and and_3 (out_7, in_2, or_2_out);
endmodule
