// Logisim project Fig 3.7.circ as structural Verilog: 1 circuit, main circuit main
module main (
  input  in_1,
  input  in_2,
  input  in_3,
  input  in_4,
  input  in_5,
  input  in_6,
  input  in_7,
  input  in_8,
  input  in_9,
  input  in_10,
  input  in_11,
  input  in_12,
  input  in_13,
  input  in_14,
  input  in_15,
  input  in_16,
  output out_17,
  output out_18,
  output out_19,
  output out_20,
  output out_21,
  output out_22,
  output out_23,
  output out_24
);

  wire not_1_out, not_2_out, not_3_out, not_4_out, not_5_out, not_6_out, not_7_out, not_8_out;

  not not_1 (not_1_out, in_5);
  not not_2 (not_2_out, in_7);
  not not_3 (not_3_out, in_13);
  not not_4 (not_4_out, in_15);
  nand nand_1 (out_17, in_1, in_3);
  or or_1 (out_19, not_1_out, not_2_out);
  nor nor_1 (out_21, in_9, in_11);
  and and_1 (out_23, not_3_out, not_4_out);
  and and_2 (out_18, in_2, in_4);
  not not_5 (not_5_out, in_6);
  nor nor_2 (out_20, not_5_out, not_6_out);
  not not_6 (not_6_out, in_8);
  or or_2 (out_22, in_10, in_12);
  not not_7 (not_7_out, in_14);
  nand nand_2 (out_24, not_7_out, not_8_out);
  not not_8 (not_8_out, in_16);
endmodule
