// Logisim project Fig 3.8.circ as structural Verilog: 1 circuit, main circuit main
module main (
  input  in_1,
  input  in_2,
  input  in_3,
  input  in_4,
  input  in_5,
  input  in_6,
  input  in_7,
  input  in_8,
  input  in_9,
  input  in_10,
  input  in_11,
  input  in_12,
  input  in_13,
  input  in_14,
  output out_15,
  output out_16,
  output out_17,
  output out_18
);

  wire and_1_out, and_2_out, nand_1_out, nand_2_out, nand_3_out, nand_4_out, not_1_out, not_2_out, not_3_out,
       not_4_out, not_5_out, not_6_out, not_7_out, not_8_out;

  not not_1 (not_1_out, in_3);
  not not_2 (not_2_out, in_6);
  not not_3 (not_3_out, in_7);
  not not_4 (not_4_out, in_10);
  not not_5 (not_5_out, in_11);
  not not_6 (not_6_out, in_14);
  xor xor_1 (out_15, in_1, in_2);
  and and_1 (and_1_out, not_1_out, in_4);
  and and_2 (and_2_out, in_5, not_2_out);
  nand nand_1 (nand_1_out, not_3_out, in_8);
  nand nand_2 (nand_2_out, in_9, not_4_out);
  nand nand_3 (nand_3_out, not_5_out, in_12);
  nand nand_4 (nand_4_out, in_13, not_6_out);
  or or_1 (out_16, and_1_out, and_2_out);
  not not_7 (not_7_out, nand_1_out);
  not not_8 (not_8_out, nand_2_out);
  or or_2 (out_17, not_7_out, not_8_out);
  nand nand_5 (out_18, nand_3_out, nand_4_out);
endmodule
