// Logisim project ula_8_bits_ivo.circ as structural Verilog: 2 circuits, main circuit ALU_8_bits
module ALU_8_bits (
  input  Su,
  input  A7,
  input  A6,
  input  A5,
  input  A4,
  input  A3,
  input  A2,
  input  A1,
  input  A0,
  input  En,
  input  B7,
  input  B6,
  input  B5,
  input  B4,
  input  B3,
  input  B2,
  input  B1,
  input  B0,
  output CF,
  output ZF,
  output S7,
  output S6,
  output S5,
  output S4,
  output S3,
  output S2,
  output S1,
  output S0,
  output E7,
  output E6,
  output E5,
  output E4,
  output E3,
  output E2,
  output E1,
  output E0
);

  wire full_adder_1_co, full_adder_2_co, full_adder_3_co, full_adder_4_co, full_adder_5_co, full_adder_6_co,
       full_adder_7_co, xor_1_out, xor_2_out, xor_3_out, xor_4_out, xor_5_out, xor_6_out, xor_7_out,
       xor_8_out;

  Full_adder full_adder_1 (.A(A1), .B(xor_7_out), .Ci(full_adder_2_co), .Co(full_adder_1_co), .E(S1));
  Full_adder full_adder_2 (.A(A0), .B(xor_8_out), .Ci(Su), .Co(full_adder_2_co), .E(S0));
  xor xor_1 (xor_1_out, Su, B7);
  Full_adder full_adder_3 (.A(A2), .B(xor_6_out), .Ci(full_adder_1_co), .Co(full_adder_3_co), .E(S2));
  xor xor_2 (xor_2_out, Su, B6);
  xor xor_3 (xor_3_out, Su, B5);
  Full_adder full_adder_4 (.A(A3), .B(xor_5_out), .Ci(full_adder_3_co), .Co(full_adder_4_co), .E(S3));
  xor xor_4 (xor_4_out, Su, B4);
  xor xor_5 (xor_5_out, Su, B3);
  Full_adder full_adder_5 (.A(A4), .B(xor_4_out), .Ci(full_adder_4_co), .Co(full_adder_5_co), .E(S4));
  Full_adder full_adder_6 (.A(A5), .B(xor_3_out), .Ci(full_adder_5_co), .Co(full_adder_6_co), .E(S5));
  xor xor_6 (xor_6_out, Su, B2);
  xor xor_7 (xor_7_out, Su, B1);
  Full_adder full_adder_7 (.A(A6), .B(xor_2_out), .Ci(full_adder_6_co), .Co(full_adder_7_co), .E(S6));
  xor xor_8 (xor_8_out, Su, B0);
  Full_adder full_adder_8 (.A(A7), .B(xor_1_out), .Ci(full_adder_7_co), .Co(CF), .E(S7));
  nor nor_1 (ZF, S7, S6, S5, S4, S3, S2, S1, S0);
  assign E7 = En ? S7 : 1'bz;  // Controlled_Buffer controlled_buffer_1
  assign E6 = En ? S6 : 1'bz;  // Controlled_Buffer controlled_buffer_2
  assign E5 = En ? S5 : 1'bz;  // Controlled_Buffer controlled_buffer_3
  assign E4 = En ? S4 : 1'bz;  // Controlled_Buffer controlled_buffer_4
  assign E3 = En ? S3 : 1'bz;  // Controlled_Buffer controlled_buffer_5
  assign E2 = En ? S2 : 1'bz;  // Controlled_Buffer controlled_buffer_6
  assign E1 = En ? S1 : 1'bz;  // Controlled_Buffer controlled_buffer_7
  assign E0 = En ? S0 : 1'bz;  // Controlled_Buffer controlled_buffer_8
endmodule

module Full_adder (
  input  A,
  input  B,
  input  Ci,
  output E,
  output Co
);

  wire and_1_out, and_2_out, xor_1_out;

  xor xor_1 (xor_1_out, A, B);
  xor xor_2 (E, xor_1_out, Ci);
  and and_1 (and_1_out, xor_1_out, Ci);
  or or_1 (Co, and_1_out, and_2_out);
  and and_2 (and_2_out, A, B);
endmodule
